# Fritzing sketch 4N36_LedTesterApp (saved by Fritzing 1.0.6)
breadboards: 1

parts:
  esp1 = ESP32 DevKitc V4
  R1 = Resistor [tolerance=±5% power=0.25W resistance=330 package=THT]
  LED1 = LED - 5mm [color="Red (633nm)" current=0.030A package="5 mm [THT]"]
  R2 = Resistor [tolerance=±5% power=0.25W resistance=470 package=THT]
  Part1 = Lilypad Power Supply
  U1 = Optocoupler [package=THT]
  U2 = Optocoupler [package=THT]
  R3 = Resistor [tolerance=±5% power=0.25W resistance=470 package=THT]
  LED2 = LED - 5mm [color="Red (633nm)" current=0.030A package="5 mm [THT]"]
  R4 = Resistor [tolerance=±5% power=0.25W resistance=330 package=THT]
  S1 = Pushbutton [package="[THT]"]
  S2 = Pushbutton [package="[THT]"]
  R5 = Resistor [tolerance=±5% power=0.25W resistance=10k package=THT]
  R6 = Resistor [tolerance=±5% power=0.25W resistance=10k package=THT]

nets:
  N1: esp1.IO18, S2.Pin_3, S2.Pin_4, R6.Pin_1
  N2: esp1.IO19, S1.Pin_3, S1.Pin_4, R5.Pin_1
  N3: esp1.3V3, S1.Pin_1, S1.Pin_2, S2.Pin_1, S2.Pin_2
  N4: esp1.IO25, R3.Pin_1
  N5: esp1.IO26, R2.Pin_1
  N6: esp1.GND#32, U1.Pin_2, U2.Pin_2, R5.Pin_0, R6.Pin_0
  N7: R1.Pin_0, LED1.cathode
  N8: R1.Pin_1, Part1.GND, U1.Pin_4, U2.Pin_4, R4.Pin_1
  N9: LED1.anode, U1.Pin_5
  N10: R2.Pin_0, U2.Pin_1
  N11: U1.Pin_1, R3.Pin_0
  N12: U2.Pin_5, LED2.anode
  N13: LED2.cathode, R4.Pin_0

custom parts:
  ESP32 DevKitc V4: ESP32-DevKitC board with ESP32-WROOM-32 module. ESP32-DevKitC V4 is a small-sized ESP32-based development board produced by Espressif. Most of the pins on the ESP module are broken out to the pin headers on the board. The pins D0, D1, D2, D3, CMD and CLK are used internally for communication between ESP32 and SPI flash memory. They are grouped on both sides near the USB connector. Avoid using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
