# Fritzing sketch CanonTrigger_withLaserSensor (saved by Fritzing 1.0.6)
breadboards: 2

parts:
  esp1 = ESP32 DevKitc V4
  R2 = Resistor [tolerance=±5% power=0.25W resistance=470 package=THT]
  U1 = Optocoupler [package=THT]
  U2 = Optocoupler [package=THT]
  R3 = Resistor [tolerance=±5% power=0.25W resistance=470 package=THT]
  S1 = Pushbutton [package="[THT]"]
  S2 = Pushbutton [package="[THT]"]
  R5 = Resistor [tolerance=±5% power=0.25W resistance=10k package=THT]
  R6 = Resistor [tolerance=±5% power=0.25W resistance=10k package=THT]
  R7 = Resistor [tolerance=±5% power=0.25W resistance=220 package=THT]
  R8 = Resistor [tolerance=±5% power=0.25W resistance=220 package=THT]
  LED3 = LED - 5mm [color="Red (633nm)" current=0.030A package="5 mm [THT]"]
  LED4 = LED - 5mm [color="Red (633nm)" current=0.030A package="5 mm [THT]"]
  Laser_Transmitter_Module1 = Laser Transmitter Module [part_number="Laser Transmitter Module" chip_label=IC package="DIP (Dual Inline) [THT]"]
  Pullup_Resistor = Resistor [tolerance=±5% power=0.25W resistance=10k package=THT]
  Laser_Sensor_Module1 = Laser Sensor Module [part_number="Laser Sensor Module" chip_label=IC package="DIP (Dual Inline) [THT]"]

nets:
  N1: esp1.IO15, R7.Pin_0
  N2: esp1.IO16, R8.Pin_0
  N3: esp1.IO18, S2.Pin_3, S2.Pin_4, R6.Pin_1
  N4: esp1.IO19, S1.Pin_3, S1.Pin_4, R5.Pin_1
  3V3: esp1.3V3, S1.Pin_1, S1.Pin_2, S2.Pin_1, S2.Pin_2, Pullup_Resistor.Pin_1, Laser_Sensor_Module1.VCC
  N5: esp1.VN, Laser_Transmitter_Module1.OUT
  N6: esp1.IO34, Pullup_Resistor.Pin_0, Laser_Sensor_Module1.OUT
  N7: esp1.IO25, R3.Pin_1
  N8: esp1.IO26, R2.Pin_1
  N9: esp1.GND#32, U1.Pin_2, U2.Pin_2, R5.Pin_0, R6.Pin_0, LED3.cathode, LED4.cathode, Laser_Transmitter_Module1.GND
  N10: R2.Pin_0, U2.Pin_1
  N11: U1.Pin_1, R3.Pin_0
  N12: U1.Pin_4, U2.Pin_4
  N13: R7.Pin_1, LED4.anode
  N14: R8.Pin_1, LED3.anode

notes:
  To the corresponding cabble of the trugger

custom parts:
  ESP32 DevKitc V4: ESP32-DevKitC board with ESP32-WROOM-32 module. ESP32-DevKitC V4 is a small-sized ESP32-based development board produced by Espressif. Most of the pins on the ESP module are broken out to the pin headers on the board. The pins D0, D1, D2, D3, CMD and CLK are used internally for communication between ESP32 and SPI flash memory. They are grouped on both sides near the USB connector. Avoid using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
  Laser Transmitter Module: Red Laser Transmitter Module Power Input: 5V DC Laser: KY-008 Wavelenght: 650nm
  Laser Sensor Module: Laser Sensor/Detector/Receiver Module Working Voltage: 5V
